# Fritzing sketch BattleClientGameServerOntwerp (saved by Fritzing 0.9.2b)
breadboards: 4

parts:
  Part1 = Arduino Uno (Rev3)
  R1 = Resistor [tolerance=±5% resistance=220 package=THT]
  R2 = Resistor [tolerance=±5% resistance=220 package=THT]
  R3 = Resistor [tolerance=±5% resistance=220 package=THT]
  R4 = Resistor [tolerance=±5% resistance=220 package=THT]
  LCD1 = LCD screen
  S1 = Pushbutton [package="[THT]"]
  S2 = Pushbutton [package="[THT]"]
  S3 = Pushbutton [package="[THT]"]
  S4 = Pushbutton [package="[THT]"]
  R5 = Trimmer Potentiometer [maximum_resistance=10kΩ package=THT]
  R6 = Resistor [tolerance=±5% resistance=220 package=THT]
  Onderdeel2 = Arduino Uno (Rev3) - ICSP
  R7 = Rotary Potentiometer (Large) [maximum_resistance=10kΩ package=THT]
  S5 = Pushbutton [package="[SMD]"]
  R8 = Resistor [tolerance=±5% resistance=220 package="0402 [SMD]"]
  LCD2 = LCD screen
  R9 = Resistor [tolerance=±5% resistance=220 package="0805 [SMD]"]
  Part2 = Arduino Uno (Rev3)
  R10 = Resistor [tolerance=±5% resistance=220 package=THT]
  R11 = Resistor [tolerance=±5% resistance=220 package=THT]
  R12 = Resistor [tolerance=±5% resistance=220 package=THT]
  R13 = Resistor [tolerance=±5% resistance=220 package=THT]
  LCD3 = LCD screen
  S6 = Pushbutton [package="[THT]"]
  S7 = Pushbutton [package="[THT]"]
  S8 = Pushbutton [package="[THT]"]
  S9 = Pushbutton [package="[THT]"]
  R14 = Trimmer Potentiometer [maximum_resistance=10kΩ package=THT]
  R15 = Resistor [tolerance=±5% resistance=220 package=THT]

nets:
  N1: Part1.A4/SDA, Part2.A4/SDA
  N2: Part1.A5/SCL, Part2.A5/SCL
  N3: Part1.D8, LCD1.DB4
  N4: Part1.D9_PWM, LCD1.DB5
  N5: Part1.D10_PWM/SS, LCD1.DB6
  N6: Part1.D11_PWM/MOSI, LCD1.DB7
  N7: Part1.D12/MISO, LCD1.RS
  N8: Part1.D13/SCK, LCD1.E
  N9: Part1.D4, R4.Pin_1, S4.Pin_1, S4.Pin_2
  N10: Part1.D5_PWM, R3.Pin_1, S3.Pin_1, S3.Pin_2
  N11: Part1.D6_PWM, R2.Pin_1, S2.Pin_1, S2.Pin_2
  N12: Part1.D7, R1.Pin_1, S1.Pin_1, S1.Pin_2
  5V: Part1.5V, LCD1.VDD, S1.Pin_3, S1.Pin_4, S2.Pin_3, S2.Pin_4, S3.Pin_3, S3.Pin_4, S4.Pin_3, S4.Pin_4, R5.leg2, R6.Pin_0
  GND: Part1.GND, R1.Pin_0, R2.Pin_0, R3.Pin_0, R4.Pin_0, LCD1.VSS, LCD1.R/W, LCD1.LED-, R5.leg1, Part2.GND, R10.Pin_0, R11.Pin_0, R12.Pin_0, R13.Pin_0, LCD3.VSS, LCD3.R/W, LCD3.LED-, R14.leg1
  N13: LCD1.V0, R5.wiper
  N14: LCD1.LED+, R6.Pin_1
  N15: Onderdeel2.D8, LCD2.DB4
  N16: Onderdeel2.D9_PWM, LCD2.DB5
  N17: Onderdeel2.D10_PWM/SS, LCD2.DB6
  N18: Onderdeel2.D11_PWM/MOSI, LCD2.DB7
  N19: Onderdeel2.D2, S5.Pin_3, S5.Pin_4, R8.Pin_1
  N20: Onderdeel2.D6_PWM, LCD2.RS
  N21: Onderdeel2.D7, LCD2.E
  N22: Onderdeel2.IOREF, R7.leg2, S5.Pin_1, S5.Pin_2, LCD2.VDD, R9.Pin_1
  GND_2: Onderdeel2.GND, R7.leg1, R8.Pin_0, LCD2.VSS, LCD2.R/W, LCD2.LED-
  N23: R7.wiper, LCD2.V0
  N24: LCD2.LED+, R9.Pin_0
  N25: Part2.D8, LCD3.DB4
  N26: Part2.D9_PWM, LCD3.DB5
  N27: Part2.D10_PWM/SS, LCD3.DB6
  N28: Part2.D11_PWM/MOSI, LCD3.DB7
  N29: Part2.D12/MISO, LCD3.RS
  N30: Part2.D13/SCK, LCD3.E
  N31: Part2.D4, R10.Pin_1, S9.Pin_1, S9.Pin_2
  N32: Part2.D5_PWM, R11.Pin_1, S8.Pin_1, S8.Pin_2
  N33: Part2.D6_PWM, R12.Pin_1, S7.Pin_1, S7.Pin_2
  N34: Part2.D7, R13.Pin_1, S6.Pin_1, S6.Pin_2
  5V_2: Part2.5V, LCD3.VDD, S6.Pin_3, S6.Pin_4, S7.Pin_3, S7.Pin_4, S8.Pin_3, S8.Pin_4, S9.Pin_3, S9.Pin_4, R14.leg2, R15.Pin_0
  N35: LCD3.V0, R14.wiper
  N36: LCD3.LED+, R15.Pin_1

notes:
  Client arduino
  Ground
  A5
  A4
  Server arduino
